# Fritzing sketch PYBOARD_20x4_DISPLAY_SCHEM (saved by Fritzing 0.9.2b)
breadboards: 1

parts:
  pyboard1 = Micro Python pyboard [part_number=PYBv10b]
  LCD1 = LCD screen
  R1 = Rotary Potentiometer (Small) [maximum_resistance=100kΩ package=THT]

nets:
  N1: pyboard1.X1, LCD1.DB0
  N2: pyboard1.X2, LCD1.DB1
  N3: pyboard1.X3, LCD1.DB2
  N4: pyboard1.X4, LCD1.DB3
  N5: pyboard1.X5, LCD1.DB4
  N6: pyboard1.X6, LCD1.DB5
  N7: pyboard1.X7, LCD1.DB6
  N8: pyboard1.X8, LCD1.DB7
  N9: pyboard1.Y9, LCD1.RS
  N10: pyboard1.Y10, LCD1.E
  N11: pyboard1.Y14_GND, LCD1.VSS, LCD1.R/W, LCD1.LED-, R1.leg2
  N12: pyboard1.Y16_VIN, LCD1.VDD, LCD1.LED+, R1.leg1
  N13: LCD1.V0, R1.wiper

notes:
  Y9
  Y10
  X1-X8 are parallel in/out to LCD
  Pot adjusts LCD contrast
  16x2 or 20x4 both work
  PWR is +5 from Pyboard USB
  GND from Pyboard
